// Logisim project stack_logical_easy.circ as structural Verilog: 10 circuits, main circuit main
module main (
  input  CLK,
  input  RESET,
  input  [1:0] COMMAND,
  input  [2:0] INDEX,
  input  [3:0] IDATA,
  output [3:0] ODATA
);

  stack stack_1 (.CLK(CLK), .RESET(RESET), .COMMAND(COMMAND), .INDEX(INDEX), .IDATA(IDATA), .ODATA(ODATA));
endmodule

module stack (
  input  CLK,
  input  RESET,
  input  [1:0] COMMAND,
  input  [2:0] INDEX,
  input  [3:0] IDATA,
  output [3:0] ODATA
);

  wire and_1_out, and_2_out, and_3_out, twodecoder_1_q1, twodecoder_1_q2, twodecoder_1_q3;

  twoDecoder twodecoder_1 (
    .in_1(COMMAND), .Q1(twodecoder_1_q1), .Q2(twodecoder_1_q2), .Q3(twodecoder_1_q3));  // open: Q0
  and and_1 (and_1_out, CLK, twodecoder_1_q1);
  and and_2 (and_2_out, CLK, twodecoder_1_q2);
  and and_3 (and_3_out, CLK, twodecoder_1_q3);
  cellue cellue_1 (
    .index(INDEX), .get(and_3_out), .inBit(IDATA[0]), .reset(RESET), .pop(and_2_out), .push(and_1_out),
    .OutBit(ODATA[0]));
  cellue cellue_2 (
    .index(INDEX), .get(and_3_out), .inBit(IDATA[1]), .reset(RESET), .pop(and_2_out), .push(and_1_out),
    .OutBit(ODATA[1]));
  cellue cellue_3 (
    .index(INDEX), .get(and_3_out), .inBit(IDATA[2]), .reset(RESET), .pop(and_2_out), .push(and_1_out),
    .OutBit(ODATA[2]));
  cellue cellue_4 (
    .index(INDEX), .get(and_3_out), .inBit(IDATA[3]), .reset(RESET), .pop(and_2_out), .push(and_1_out),
    .OutBit(ODATA[3]));

  // Other names for the same wires on the sheet: inData[3:0] = IDATA; OutData[3:0] = ODATA

  // Notes on the sheet:
  //   your circuit must be here
endmodule

module DTrigger (
  input  D,
  input  C,
  input  Reset,
  output Q
);

  wire and_1_out, and_2_out, nor_2_out, not_1_out, or_1_out;

  not not_1 (not_1_out, D);
  and and_1 (and_1_out, not_1_out, C);
  and and_2 (and_2_out, D, C);
  nor nor_1 (Q, and_1_out, or_1_out);
  nor nor_2 (nor_2_out, and_2_out, Q);
  or or_1 (or_1_out, nor_2_out, Reset);
endmodule

module threeDecoder (
  input  [2:0] num,
  output Q0,
  output Q1,
  output Q2,
  output Q3,
  output Q4,
  output Q5,
  output Q6,
  output Q7
);

  wire not_1_out, not_2_out, not_3_out;

  not not_1 (not_1_out, num[0]);
  not not_2 (not_2_out, num[1]);
  not not_3 (not_3_out, num[2]);
  and and_1 (Q0, not_1_out, not_2_out, not_3_out);
  and and_2 (Q1, num[0], not_2_out, not_3_out);
  and and_3 (Q2, not_1_out, num[1], not_3_out);
  and and_4 (Q3, num[0], num[1], not_3_out);
  and and_5 (Q4, not_1_out, not_2_out, num[2]);
  and and_6 (Q5, num[0], not_2_out, num[2]);
  and and_7 (Q6, not_1_out, num[1], num[2]);
  and and_8 (Q7, num[0], num[1], num[2]);
endmodule

module cellue (
  input  [2:0] index,
  input  get,
  input  inBit,
  input  reset,
  input  pop,
  input  push,
  output OutBit
);

  wire and_1_out, and_2_out, and_3_out, and_4_out, and_5_out, convert_1_q, convert_2_q, convert_3_q,
       convert_4_q, convert_5_q, littlecellue_1_q0, littlecellue_1_q1, littlecellue_1_q2, littlecellue_1_q3,
       littlecellue_1_q4, mux_1_q, not_1_out, or_1_out, or_2_out, popCellue_q0, popCellue_q1, popCellue_q2,
       popCellue_q3, popCellue_q4, pushCellue_q0, pushCellue_q1, pushCellue_q2, pushCellue_q3, pushCellue_q4;

  or or_1 (or_1_out, pop, push);
  not not_1 (not_1_out, or_1_out);
  littleCellue littlecellue_1 (
    .D0(convert_1_q), .D1(convert_2_q), .D2(convert_3_q), .D3(convert_4_q), .D4(convert_5_q), .C(or_1_out),
    .Reset(reset), .Q0(littlecellue_1_q0), .Q1(littlecellue_1_q1), .Q2(littlecellue_1_q2),
    .Q3(littlecellue_1_q3), .Q4(littlecellue_1_q4));
  MUX mux_1 (
    .num(index), .D0(littlecellue_1_q0), .D1(littlecellue_1_q1), .D2(littlecellue_1_q2),
    .D3(littlecellue_1_q3), .D4(littlecellue_1_q4), .q(mux_1_q));
  and and_1 (and_1_out, or_1_out, inBit);
  and and_2 (and_2_out, not_1_out, pushCellue_q0);
  and and_3 (and_3_out, get, mux_1_q);
  littleCellue pushCellue (
    .D0(littlecellue_1_q4), .D1(littlecellue_1_q0), .D2(littlecellue_1_q1), .D3(littlecellue_1_q2),
    .D4(littlecellue_1_q3), .C(not_1_out), .Reset(reset), .Q0(pushCellue_q0), .Q1(pushCellue_q1),
    .Q2(pushCellue_q2), .Q3(pushCellue_q3), .Q4(pushCellue_q4));
  littleCellue popCellue (
    .D0(littlecellue_1_q1), .D1(littlecellue_1_q2), .D2(littlecellue_1_q3), .D3(littlecellue_1_q4),
    .D4(littlecellue_1_q0), .C(not_1_out), .Reset(reset), .Q0(popCellue_q0), .Q1(popCellue_q1),
    .Q2(popCellue_q2), .Q3(popCellue_q3), .Q4(popCellue_q4));
  or or_2 (or_2_out, and_1_out, and_2_out);
  and and_4 (and_4_out, pushCellue_q1, pop);
  and and_5 (and_5_out, or_2_out, push);
  or or_3 (OutBit, and_3_out, and_5_out, and_4_out);
  convert convert_1 (.PushQ(or_2_out), .Push(push), .Pop(pop), .PopQ(popCellue_q0), .Q(convert_1_q));
  convert convert_2 (.PushQ(pushCellue_q1), .Push(push), .Pop(pop), .PopQ(popCellue_q1), .Q(convert_2_q));
  convert convert_3 (.PushQ(pushCellue_q2), .Push(push), .Pop(pop), .PopQ(popCellue_q2), .Q(convert_3_q));
  convert convert_4 (.PushQ(pushCellue_q3), .Push(push), .Pop(pop), .PopQ(popCellue_q3), .Q(convert_4_q));
  convert convert_5 (.PushQ(pushCellue_q4), .Push(push), .Pop(pop), .PopQ(popCellue_q4), .Q(convert_5_q));
endmodule

module littleCellue (
  input  D0,
  input  D1,
  input  D2,
  input  D3,
  input  D4,
  input  C,
  input  Reset,
  output Q0,
  output Q1,
  output Q2,
  output Q3,
  output Q4
);

  DTrigger dtrigger_1 (.D(D0), .C(C), .Reset(Reset), .Q(Q0));
  DTrigger dtrigger_2 (.D(D1), .C(C), .Reset(Reset), .Q(Q1));
  DTrigger dtrigger_3 (.D(D2), .C(C), .Reset(Reset), .Q(Q2));
  DTrigger dtrigger_4 (.D(D3), .C(C), .Reset(Reset), .Q(Q3));
  DTrigger dtrigger_5 (.D(D4), .C(C), .Reset(Reset), .Q(Q4));
endmodule

module convert (
  input  PushQ,
  input  Push,
  input  Pop,
  input  PopQ,
  output Q
);

  wire and_1_out, and_2_out;

  and and_1 (and_1_out, PushQ, Push);
  and and_2 (and_2_out, Pop, PopQ);
  or or_1 (Q, and_1_out, and_2_out);
endmodule

module twoDecoder (
  input  [1:0] in_1,
  output Q0,
  output Q1,
  output Q2,
  output Q3
);

  wire not_1_out, not_2_out;

  not not_1 (not_1_out, in_1[0]);
  not not_2 (not_2_out, in_1[1]);
  and and_1 (Q0, not_1_out, not_2_out);
  and and_2 (Q1, in_1[0], not_2_out);
  and and_3 (Q2, in_1[1], not_1_out);
  and and_4 (Q3, in_1[1], in_1[0]);
endmodule

module MUX (
  input  [2:0] num,
  input  D0,
  input  D1,
  input  D2,
  input  D3,
  input  D4,
  output q
);

  wire and_1_out, and_2_out, and_3_out, and_4_out, and_5_out, threedecoder_1_q0, threedecoder_1_q1,
       threedecoder_1_q2, threedecoder_1_q3, threedecoder_1_q4;

  threeDecoder threedecoder_1 (
    .num(num), .Q0(threedecoder_1_q0), .Q1(threedecoder_1_q1), .Q2(threedecoder_1_q2),
    .Q3(threedecoder_1_q3), .Q4(threedecoder_1_q4));  // open: Q5, Q6, Q7
  and and_1 (and_1_out, threedecoder_1_q0, D0);
  and and_2 (and_2_out, threedecoder_1_q1, D1);
  and and_3 (and_3_out, threedecoder_1_q2, D2);
  and and_4 (and_4_out, threedecoder_1_q3, D3);
  and and_5 (and_5_out, threedecoder_1_q4, D4);
  or or_1 (q, and_1_out, and_2_out, and_3_out, and_4_out, and_5_out);
endmodule

module DD_Trigger (
  input  D,
  input  C,
  input  Reset,
  output Q
);

  wire dtrigger_1_q, not_1_out;

  not not_1 (not_1_out, C);
  DTrigger dtrigger_1 (.D(D), .C(not_1_out), .Reset(Reset), .Q(dtrigger_1_q));
  DTrigger dtrigger_2 (.D(dtrigger_1_q), .C(C), .Reset(Reset), .Q(Q));
endmodule
